// Logisim project SAP2.circ as structural Verilog: 3 circuits, main circuit main
module main (
  input  [7:0] in_1,
  input  in_2,
  input  in_3,
  input  in_4,
  input  in_5,
  input  in_6,
  input  in_7,
  input  in_8,
  input  in_9,
  input  in_10,
  input  in_11,
  input  in_12,
  input  in_13,
  input  in_14,
  input  in_15,
  input  in_16,
  input  in_17,
  input  in_18,
  input  in_19,
  input  in_20,
  input  in_21,
  input  in_22,
  input  in_23,
  input  in_24,
  input  in_25,
  input  in_26,
  input  in_27,
  input  in_28,
  input  in_29,
  input  in_30,
  input  in_31,
  input  in_32,
  output [14:0] pc_data,
  output [14:0] Memory_Address
);

  wire and_1_out, CF, clk, clock_1_out, not_1_out, not_2_out, rst, ZF;
  wire [7:0] ALU_data_p1, controlled_buffer_1_out, controlled_buffer_2_out, ram_1_data, REG_A_q, REG_B_q,
       REG_C_q, REG_D_q;
  wire [7:7] MAR_H_q;

  Clock clock_1 (.out(clock_1_out));
  and and_1 (and_1_out, clock_1_out, not_1_out);
  not not_1 (not_1_out, rst);
  not not_2 (not_2_out, in_4);
  Register MAR_L (.D(controlled_buffer_1_out), .en(in_3), .clk(clk), .Q(Memory_Address[7:0]), .clr(in_6));
  Register MAR_H (
    .D(controlled_buffer_2_out), .en(in_8), .clk(clk), .Q({MAR_H_q[7], Memory_Address[14:8]}), .clr(in_10));
  RAM #(.addrWidth(15), .asyncread("true"), .databus("bidir"), .\type ("nonvolatile")) ram_1 (
    .addr(Memory_Address), .we(in_7), .oe(in_9), .clk(clk), .data(ram_1_data));
  Button Reset (.out(rst));
  and and_2 (clk, and_1_out, not_2_out);
  // LedBar #(.inputtype("row")) ledbar_1: pin names not known; wires that end beside it: ram_1_data
  assign controlled_buffer_1_out = in_2 ? ram_1_data : 8'bz;  // Controlled_Buffer controlled_buffer_1
  assign controlled_buffer_2_out = in_5 ? ram_1_data : 8'bz;  // Controlled_Buffer controlled_buffer_2
  assign ram_1_data = in_1;  // Buffer buffer_1, 8 bits wide
  Program_Counter program_counter_1 (
    .clk(clk), .pc_L_out(in_31), .pc_H_out(in_32), .pc_L_in(in_29), .pc_H_in(in_30), .pc_en(in_27),
    .pc_clr(in_28), .bus_in(ram_1_data), .pc_info(pc_data), .pc_out(ram_1_data));
  Pull_Resistor pull_resistor_1 (.node(ram_1_data));
  // LedBar #(.inputtype("row")) ALU_data: pin names not known; wires that end beside it: ALU_data_p1
  ALU alu_1 (
    .SU(in_16), .B_in(REG_B_q), .A_in(REG_A_q), .FLAG_in(in_19), .clk(clk), .FLAG_clr(in_22), .EO(in_13),
    .ALU_out(ram_1_data), .ALU_data(ALU_data_p1), .CF(CF), .ZF(ZF));
  Register REG_A (.D(ram_1_data), .en(in_11), .clk(clk), .Q(REG_A_q), .clr(in_17));
  Register REG_B (.D(ram_1_data), .en(in_20), .clk(clk), .Q(REG_B_q), .clr(in_25));
  Register REG_C (.D(ram_1_data), .en(in_12), .clk(clk), .Q(REG_C_q), .clr(in_18));
  Register REG_D (.D(ram_1_data), .en(in_21), .clk(clk), .Q(REG_D_q), .clr(in_26));
  assign ram_1_data = in_14 ? REG_A_q : 8'bz;  // Controlled_Buffer controlled_buffer_3
  assign ram_1_data = in_23 ? REG_B_q : 8'bz;  // Controlled_Buffer controlled_buffer_4
  assign ram_1_data = in_15 ? REG_C_q : 8'bz;  // Controlled_Buffer controlled_buffer_5
  // LedBar #(.inputtype("row")) A_data: pin names not known; wires that end beside it: REG_A_q
  // LedBar #(.inputtype("row")) B_data: pin names not known; wires that end beside it: REG_B_q
  assign ram_1_data = in_24 ? REG_D_q : 8'bz;  // Controlled_Buffer controlled_buffer_6

  // Other names for the same wires on the sheet: A_clr = in_17; A_in = in_11; A_out = in_14; B_clr = in_25;
  //   B_in = in_20; B_out = in_23; C_clr = in_18; C_in = in_12; C_out = in_15; D_clr = in_26; D_in = in_21;
  //   D_out = in_24; EO = in_13; FLAG_clr = in_22; FLAG_in = in_19; hlt = in_4; mar_H_in = in_5; mar_H_rst = in_10;
  //   mar_H_wrt = in_8; mar_L_in = in_2; mar_L_rst = in_6; mar_L_wrt = in_3; PC_clr = in_28; PC_en = in_27;
  //   pc_H_in = in_30; pc_H_out = in_32; pc_L_in = in_29; pc_L_out = in_31; ram_in = in_7; ram_out = in_9; SU = in_16

  // Notes on the sheet:
  //   in_7: pull=down
  //   in_9: pull=down
  //   in_2: pull=down
  //   in_5: pull=down
  //   in_8: pull=down
  //   in_10: pull=down
  //   in_3: pull=down
  //   in_6: pull=down
  //   pc_data: pull=up
  //   in_4: pull=down
  //   Clock Unit
  //   buffer_1 drives only 1 and floats otherwise
  //   TODO:
  //   Create Real Flags Register
  //   Add support for interrupts and I/O
endmodule

module ALU (
  input  SU,
  input  [7:0] B_in,
  input  [7:0] A_in,
  input  EO,
  input  FLAG_in,
  input  clk,
  input  FLAG_clr,
  output [7:0] ALU_data,
  output [7:0] ALU_out,
  output CF,
  output ZF
);

  wire [1:0] adder_1_cout;
  wire [7:0] bit_extender_1_out, xor_1_out;

  assign bit_extender_1_out = {{7{SU}}, SU};  // Bit_Extender bit_extender_1
  assign xor_1_out = bit_extender_1_out ^ B_in;  // XOR_Gate xor_1, 8 bits wide
  Adder adder_1 (.a(xor_1_out), .b(A_in), .out(ALU_data), .cin(SU), .cout(adder_1_cout[0]));
  nor nor_1 (adder_1_cout[1], ALU_data[0], ALU_data[1], ALU_data[2], ALU_data[3], ALU_data[4], ALU_data[5], ALU_data[6], ALU_data[7]);
  assign ALU_out = EO ? ALU_data : 8'bz;  // Controlled_Buffer controlled_buffer_1
  Register #(.width(2)) Flags (.D(adder_1_cout), .en(FLAG_in), .clk(clk), .Q({ZF, CF}), .clr(FLAG_clr));

  // Notes on the sheet:
  //   SU: pull=down
  //   EO: pull=down
  //   CF: pull=down
  //   ZF: pull=down
  //   Hook up for led bar display to
  //   show internal alu state
  //   Actual controlled alu bus output
  //   ALU Flags
endmodule

module Program_Counter (
  input  pc_L_in,
  input  pc_H_in,
  input  pc_en,
  input  pc_clr,
  input  clk,
  input  pc_L_out,
  input  pc_H_out,
  output [7:0] bus_in,
  output [14:0] pc_info,
  output [7:0] pc_out
);

  wire or_1_out;
  wire [7:7] pull_resistor_2_node;
  wire [14:0] controlled_buffer_1_out;

  Pull_Resistor pull_resistor_1 (.node(bus_in));
  assign controlled_buffer_1_out = pc_L_in ? {pc_info[14:8], bus_in} : 15'bz;  // Controlled_Buffer controlled_buffer_1
  assign controlled_buffer_1_out = pc_H_in ? {bus_in[6:0], pc_info[7:0]} : 15'bz;  // Controlled_Buffer controlled_buffer_2
  or or_1 (or_1_out, pc_L_in, pc_H_in);
  Counter #(.max('h7fff), .width(15)) counter_1 (
    .load(or_1_out), .D(controlled_buffer_1_out), .count(pc_en), .Q(pc_info), .up(1'b1), .clk(clk),
    .clr(pc_clr));  // open: carry
  // LedBar #(.inputtype("row"), .matrixcols(15)) PC_Data: pin names not known; wires that end beside it: pc_info
  Pull_Resistor pull_resistor_2 (.node(pull_resistor_2_node[7]));
  assign pc_out = pc_L_out ? pc_info[7:0] : 8'bz;  // Controlled_Buffer controlled_buffer_3
  assign pc_out = pc_H_out ? {pull_resistor_2_node[7], pc_info[14:8]} : 8'bz;  // Controlled_Buffer controlled_buffer_4
  Pull_Resistor pull_resistor_3 (.node(pc_out));

  // Other names for the same wires on the sheet: pc_H_data[6:0] = pc_info[14:8]; pc_L_data[7:0] = pc_info[7:0]

  // Notes on the sheet:
  //   pc_info: pull=down
  //   pc_out: pull=down
endmodule
